# Fritzing sketch zutrittssystem_ Elektro-Schema (saved by Fritzing 1.0.1rc)

parts:
  Bauteil2 = Arduino Mega 2560 (Rev3)
  Part3 = RFID-RC522 [part_number=101218]
  Keypad4x1 = Keypad Membran 4x4
  A1 = BBAA100043
  J3 = Basic Servo

nets:
  GND: Bauteil2.GND, Part3.GND, A1.pin4, J3.gnd
  N1: Bauteil2.D13_PWM, J3.pulse
  N2: Bauteil2.D12_PWM, A1.pin1
  N3: Bauteil2.D11_PWM, A1.pin3
  N4: Bauteil2.D10_PWM, Keypad4x1.Pin1
  N5: Bauteil2.D9_PWM, Keypad4x1.Pin2
  N6: Bauteil2.D8_PWM, Keypad4x1.Pin3
  3V3: Bauteil2.3V3, Part3.3.3V
  5V: Bauteil2.5V, J3.vcc
  N7: Bauteil2.D2_PWM, Part3.RST
  N8: Bauteil2.D3_PWM, Keypad4x1.Pin8
  N9: Bauteil2.D4_PWM, Keypad4x1.Pin7
  N10: Bauteil2.D5_PWM, Keypad4x1.Pin6
  N11: Bauteil2.D6_PWM, Keypad4x1.Pin5
  N12: Bauteil2.D7_PWM, Keypad4x1.Pin4
  N13: Bauteil2.D50, Part3.MISO
  N14: Bauteil2.D51, Part3.MOSI
  N15: Bauteil2.D52, Part3.SCK
  N16: Bauteil2.D53, Part3.SDA

custom parts:
  Keypad Membran 4x4: Membrane Keypad 4x4 Matrix
  BBAA100043: BBAA100043 traffic light module.
